# Fritzing sketch multi-mcu-serial (saved by Fritzing 0.9.10b)

parts:
  Raspberry_Pi_4 = Raspberry Pi 4B
  Part1 = Adafruit ItsyBitsy nRF52840 [part_number="Adafruit #4481"]

nets:
  GND: Raspberry_Pi_4.GND, Part1.GND
  N1: Raspberry_Pi_4.GPIO14, Part1.RX
  N2: Raspberry_Pi_4.GPIO15, Part1.TX

custom parts:
  Adafruit ItsyBitsy nRF52840: What's smaller than a Feather but larger than a Trinket? It's an Adafruit ItsyBitsy nRF52840 Express featuring the Nordic nRF52840 Bluetooth LE processor! Teensy & powerful, with an fast nRF52840 Cortex M4 processor running at 64 MHz and 1 MB of FLASH - this microcontroller board is perfect when you want something very compact, with a heap-load of memory and Bluetooth LE support This Itsy is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
